# Fritzing sketch simon_says (saved by Fritzing 1.0.5)
breadboards: 1

parts:
  part = Raspberry Pi Pico or Pico 2 [part_number="Pico 2"]
  S2 = Momentary Switch [part_number=blue package=ksa_sealed_tac_switch]
  S3 = Momentary Switch [part_number=yellow package=ksa_sealed_tac_switch]
  S4 = Momentary Switch [package=ksa_sealed_tac_switch]
  S5 = Momentary Switch [part_number=green package=ksa_sealed_tac_switch]
  R3 = Resistor [tolerance=±5% power=0.25 resistance=330 package=THT]
  LED1 = LED - 3mm [color="Blue (430nm)" current=0.030 package="3 mm [THT]"]
  R6 = Resistor [tolerance=±5% power=0.25 resistance=330 package=THT]
  passive_buzzer = Piezo Buzzer [part_number=polarity!]
  LED2 = LED - 3mm [color="Red (633nm)" current=0.030 package="3 mm [THT]"]
  R7 = Resistor [tolerance=±5% power=0.25 resistance=330 package=THT]
  R8 = Resistor [tolerance=±5% power=0.25 resistance=330 package=THT]
  LED3 = LED - 3mm [color="Yellow (585nm)" current=0.030 package="3 mm [THT]"]
  LED4 = LED - 3mm [color="Green (555nm)" current=0.030 package="3 mm [THT]"]
  OLED1 = SSD1306 0.96in 128x64 I2C Monochrome OLED Display
  S1 = Momentary Switch [part_number=reset package=ksa_sealed_tac_switch]

nets:
  N1: part.pin_3, part.pin_8, part.pin_13, part.pin_18, part.pin_23, part.pin_28, part.pin_33, part.pin_38, part.pin_42, S2.1, S2.2, S3.1, S3.2, S4.1, S4.2, S5.1, S5.2, R3.Pin_0, R6.Pin_0, passive_buzzer.pin_2, R7.Pin_0, R8.Pin_0, OLED1.GND, S1.1, S1.2
  N2: part.pin_9, passive_buzzer.pin_1
  N3: part.pin_11, S5.3, S5.4
  N4: part.pin_12, S4.3, S4.4
  N5: part.pin_14, S3.3, S3.4
  N6: part.pin_15, S2.3, S2.4
  N7: part.pin_16, LED1.anode
  N8: part.pin_17, LED2.anode
  N9: part.pin_19, LED3.anode
  N10: part.pin_20, LED4.anode
  N11: part.pin_21, OLED1.SDA
  N12: part.pin_22, OLED1.SCL
  N13: part.pin_30, S1.3, S1.4
  N14: part.pin_36, OLED1.VCC
  N15: R3.Pin_1, LED1.cathode
  N16: R6.Pin_1, LED4.cathode
  N17: LED2.cathode, R8.Pin_1
  N18: R7.Pin_1, LED3.cathode

custom parts:
  Raspberry Pi Pico or Pico 2: Raspberry Pi Pico and Pico 2. Based around the RP2040 and RP2350 microcontrollers respectively, Picos are low cost microcontroller device bringing Raspberry Pi quality, cost, and easy of use to the microcontroller space. Jan 2021, Split part in to two versions: tht (this one) and SMD. This one will drill holes for a .1 in header in pcb to allow plugging in the module as well as providing pads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
  Piezo Buzzer: Part from https://www.nutsvolts.com/magazine/article/november2012_SmileysWorkshop. Breadboard and icon images modified to be 0.3" in spacing and be more similar to the actual physical part.
